# Fritzing sketch RGB (saved by Fritzing 0.7.3b)
breadboards: 1

parts:
  R1 = Rotary Potentiometer (Small) [maximum_resistance=100kΩ]
  R = Rotary Potentiometer (Small) [maximum_resistance=100kΩ]
  R3 = Rotary Potentiometer (Small) [maximum_resistance=100kΩ]
  Arduino_Ethernet_Shield1 = Arduino Ethernet Shield

nets:
  N1: R1.leg1, R.leg1, R3.leg1, Arduino_Ethernet_Shield1.GND
  N2: R1.wiper, Arduino_Ethernet_Shield1.A1
  N3: R1.leg2, R.leg2, R3.leg2, Arduino_Ethernet_Shield1.+5V
  N4: R.wiper, Arduino_Ethernet_Shield1.A0
  N5: R3.wiper, Arduino_Ethernet_Shield1.A2
